# Fritzing sketch Arduino_car (saved by Fritzing 0.9.3b)
breadboards: 1

parts:
  Arduino_Uno = Arduino Uno (Rev3)
  R-_Resistor = L293D [package=THT]
  Dc_Motor_R = DC Motor
  Dc_Motor_L = DC Motor
  Power_Supply = Battery block 9V
  Buzzer = Piezo Speaker  # not connected
  HC-05_Bluetooth_module = Bluetooth HC-05 Macho
  Blue_Led = LEDs [package=led10mm]
  Red_Led = LEDs [package=led10mm]
  R1 = Resistor [tolerance=±5% resistance=220 package="0402 [SMD]"]
  R2 = Resistor [tolerance=±5% resistance=220 package="0402 [SMD]"]
  R3 = Resistor [tolerance=±5% resistance=220 package="0402 [SMD]"]
  Logic_Level_Converter_3_3V_5V_TTL = Logic Level Converter

nets:
  N1: Arduino_Uno.D8, R-_Resistor.In_4
  N2: Arduino_Uno.D9_PWM, R1.Pin_1
  N3: Arduino_Uno.D10_PWM/SS, R2.Pin_1
  N4: Arduino_Uno.D11_PWM/MOSI, R3.Pin_0
  N5: Arduino_Uno.D0/RX, HC-05_Bluetooth_module.TXD
  N6: Arduino_Uno.D1/TX, Logic_Level_Converter_3_3V_5V_TTL.TX_HV
  N7: Arduino_Uno.D3_PWM, R-_Resistor.In_1
  N8: Arduino_Uno.D4, R-_Resistor.In_2
  N9: Arduino_Uno.D5_PWM, R-_Resistor.Enable_1
  N10: Arduino_Uno.D6_PWM, R-_Resistor.Enable_2
  N11: Arduino_Uno.D7, R-_Resistor.In_3
  5V: Arduino_Uno.5V, R-_Resistor.+V, HC-05_Bluetooth_module.VCC
  GND: Arduino_Uno.GND, R-_Resistor.0V, Power_Supply.-, HC-05_Bluetooth_module.GND, Blue_Led.C, Red_Led.C
  N12: Arduino_Uno.VIN, R-_Resistor.+Vmotor, Power_Supply.+
  N13: R-_Resistor.Out_1_(_Controlled_by_Enable_1_), Dc_Motor_R.pin_2
  N14: R-_Resistor.Out_2_(_Controlled_by_Enable_1_), Dc_Motor_R.pin_1
  N15: R-_Resistor.Out_3_(_Controlled_by_Enable_2_), Dc_Motor_L.pin_2
  N16: R-_Resistor.Out_4_(_Controlled_by_Enable_2_), Dc_Motor_L.pin_1
  N17: HC-05_Bluetooth_module.RXD, Logic_Level_Converter_3_3V_5V_TTL.TX_LV

notes:
  R 100 Ω
  R 220 Ω
